# Fritzing sketch Circuito_guante - v2 (saved by Fritzing 1.0.5)
perfboards: 1

parts:
  R1 = Basic Flex Resistor  # not connected
  R2 = Basic Flex Resistor  # not connected
  Componente1 = Analog Digital MUX Breakout
  Componente2 = ADS1115
  A1 = Esp32-c3 super mini
  R3 = Basic Flex Resistor  # not connected
  R4 = Basic Flex Resistor  # not connected
  R5 = Basic Flex Resistor  # not connected
  R6 = Resistor [tolerance=±5% resistance=220 package="0805 [SMD]"]
  R7 = Resistor [tolerance=±5% resistance=220 package="0805 [SMD]"]
  R8 = Resistor [tolerance=±5% resistance=220 package="0805 [SMD]"]
  R9 = Resistor [tolerance=±5% resistance=220 package="0805 [SMD]"]  # not connected
  R10 = Resistor [tolerance=±5% resistance=220 package="0805 [SMD]"]
  R11 = Basic Flex Resistor
  R12 = Basic Flex Resistor
  R13 = Resistor [tolerance=±5% resistance=220 package="0805 [SMD]"]
  R14 = Resistor [tolerance=±5% resistance=220 package="0805 [SMD]"]
  Componente3 = Analog Digital MUX Breakout
  R15 = Rotary Potentiometer (Small) [maximum_resistance=100kΩ knob_status=50% power=0.5W package=THT]
  R16 = Rotary Potentiometer (Small) [maximum_resistance=100kΩ knob_status=50% power=0.5W package=THT]
  R17 = Rotary Potentiometer (Small) [maximum_resistance=100kΩ knob_status=50% power=0.5W package=THT]
  R18 = Rotary Potentiometer (Small) [maximum_resistance=100kΩ knob_status=50% power=0.5W package=THT]  # not connected
  R19 = Rotary Potentiometer (Small) [maximum_resistance=100kΩ knob_status=50% power=0.5W package=THT]
  R20 = Rotary Potentiometer (Small) [maximum_resistance=100kΩ knob_status=50% power=0.5W package=THT]
  R21 = Rotary Potentiometer (Small) [maximum_resistance=100kΩ knob_status=50% power=0.5W package=THT]
  R22 = Rotary Potentiometer (Small) [maximum_resistance=100kΩ knob_status=50% power=0.5W package=THT]
  R23 = Rotary Potentiometer (Small) [maximum_resistance=100kΩ knob_status=50% power=0.5W package=THT]
  R24 = Rotary Potentiometer (Small) [maximum_resistance=100kΩ knob_status=50% power=0.5W package=THT]
  C2 = Capacitor [package=cap-pth-small2]  # not connected
  C3 = Capacitor [package=cap-pth-small2]  # not connected
  R25 = Rotary Potentiometer (Small) [maximum_resistance=100kΩ knob_status=50% power=0.5W package=THT]  # not connected
  TP1 = TP4056 [chip_label=TP4056 package="DIP (Dual Inline) [THT]"]
  U1 = LIPO-1000mAh [package=lipo-1000]  # not connected
  A2 = battery capcity indicator module 1s-8s [package=THT]
  S1 = Round Pushbutton
  S2 = Round Pushbutton  # not connected
  S3 = Round Pushbutton  # not connected
  R26 = Resistor [tolerance=±5% resistance=220 package="1206 [SMD]"]
  LED1 = LED - 3mm [color="Red (633nm)" current=0.030A package="3 mm [THT]"]
  R27 = Resistor [tolerance=±5% resistance=220 package="1206 [SMD]"]
  R28 = Resistor [tolerance=±5% resistance=220 package="1206 [SMD]"]
  R29 = Basic Flex Resistor
  R30 = Resistor [tolerance=±5% resistance=220 package="0805 [SMD]"]
  S4 = Round Pushbutton  # not connected
  LED2 = LED - 3mm [color="Red (633nm)" current=0.030A package="3 mm [THT]"]  # not connected
  R31 = Resistor [tolerance=±5% resistance=220 package="1206 [SMD]"]  # not connected
  LED3 = LED - 3mm [color="Red (633nm)" current=0.030A package="3 mm [THT]"]  # not connected
  LED4 = LED - 3mm [color="Red (633nm)" current=0.030A package="3 mm [THT]"]  # not connected
  R32 = Resistor [tolerance=±5% resistance=220 package="1206 [SMD]"]  # not connected
  R33 = Resistor [tolerance=±5% resistance=220 package="1206 [SMD]"]  # not connected

nets:
  N1: Componente1.C1, R10.Pin_0
  N2: Componente1.C2, R8.Pin_0
  N3: Componente1.C4, R6.Pin_0
  N4: Componente1.C7, R20.wiper
  N5: Componente1.C8, R24.wiper
  N6: Componente1.C9, R21.wiper
  N7: Componente1.C10, R23.wiper
  N8: Componente1.C11, R22.wiper
  N9: Componente1.C13, R7.Pin_0
  N10: Componente1.S0, A1.Pin_6
  N11: Componente1.S1, A1.Pin_11
  N12: Componente1.S2, A1.Pin_12
  N13: Componente1.SIG, Componente2.A0
  N14: Componente2.SDA, A1.Pin_4
  N15: Componente2.A1, Componente3.SIG
  N16: R11.Pin_1, R13.Pin_0
  N17: R12.Pin_1, R14.Pin_0
  N18: Componente3.C1, R19.wiper
  N19: Componente3.C3, R16.wiper
  N20: Componente3.C4, R15.wiper
  N21: Componente3.C5, R17.wiper
  N22: TP1.pin6, R27.Pin_0
  N23: A2.pin1, S1.leg1
  N24: R26.Pin_0, LED1.anode
  N25: R27.Pin_1, R28.Pin_0
  N26: R29.Pin_2, R30.Pin_0

notes:
  Circuito guante
  D1
  D2
  D3
  D4
  D5
  M1
  M2
  P0
  P1
  P2
  P3
  P4
  P5
  Ads1115
  CD74hc4067
  ESP32-C3
  POTENCIOMETROS
  SENSORES FLEX DEDOS
  NOTA: P5 opcional (mov rotacional de muñeca)
  En caso de utilizarse se necesita otro PCA9685
  SENSORES FLEX MUÑECA
  SENSORES MOVIMIENTO DE ABDUCCION
  TP4056 + Step-Up
  3,7 v - 1000 mAh
  5 v
  Encendido
  10 kΩ

custom parts:
  ADS1115: ADC ADS1115
  Esp32-c3 super mini: ESP32-C3 Development Board ESP32 SuperMini Development Board ESP32 Development Board WiFi Bluetooth.
  TP4056: A DIP stand-in part for whatever IC you want. With 6 pins on a 300mil dual inline package (DIP) footprint.
  battery capcity indicator module 1s-8s: battery capcity indicator module 1s-8s.
