# Fritzing sketch Circuito_guante (saved by Fritzing 1.0.5)

parts:
  R1 = Basic Flex Resistor
  R2 = Basic Flex Resistor
  Componente1 = Analog Digital MUX Breakout
  Componente2 = ADS1115
  A1 = Esp32-c3 super mini
  R3 = Basic Flex Resistor
  R4 = Basic Flex Resistor
  R5 = Basic Flex Resistor
  R6 = Resistor [tolerance=±5% resistance=220 package="0805 [SMD]"]
  R7 = Resistor [tolerance=±5% resistance=220 package="0805 [SMD]"]
  R8 = Resistor [tolerance=±5% resistance=220 package="0805 [SMD]"]
  R9 = Resistor [tolerance=±5% resistance=220 package="0805 [SMD]"]
  R10 = Resistor [tolerance=±5% resistance=220 package="0805 [SMD]"]
  R11 = Basic Flex Resistor
  R12 = Basic Flex Resistor
  R13 = Resistor [tolerance=±5% resistance=220 package="0805 [SMD]"]
  R14 = Resistor [tolerance=±5% resistance=220 package="0805 [SMD]"]
  Componente3 = Analog Digital MUX Breakout
  R15 = Rotary Potentiometer (Small) [maximum_resistance=100kΩ knob_status=50% power=0.5W package=THT]
  R16 = Rotary Potentiometer (Small) [maximum_resistance=100kΩ knob_status=50% power=0.5W package=THT]
  R17 = Rotary Potentiometer (Small) [maximum_resistance=100kΩ knob_status=50% power=0.5W package=THT]
  R18 = Rotary Potentiometer (Small) [maximum_resistance=100kΩ knob_status=50% power=0.5W package=THT]
  R19 = Rotary Potentiometer (Small) [maximum_resistance=100kΩ knob_status=50% power=0.5W package=THT]
  R20 = Rotary Potentiometer (Small) [maximum_resistance=100kΩ knob_status=50% power=0.5W package=THT]
  R21 = Rotary Potentiometer (Small) [maximum_resistance=100kΩ knob_status=50% power=0.5W package=THT]
  R22 = Rotary Potentiometer (Small) [maximum_resistance=100kΩ knob_status=50% power=0.5W package=THT]
  R23 = Rotary Potentiometer (Small) [maximum_resistance=100kΩ knob_status=50% power=0.5W package=THT]
  R24 = Rotary Potentiometer (Small) [maximum_resistance=100kΩ knob_status=50% power=0.5W package=THT]
  C2 = Capacitor [package=cap-pth-small2]
  C3 = Capacitor [package=cap-pth-small2]
  R25 = Rotary Potentiometer (Small) [maximum_resistance=100kΩ knob_status=50% power=0.5W package=THT]
  TP1 = TP4056 [chip_label=TP4056 package="DIP (Dual Inline) [THT]"]
  U1 = LIPO-1000mAh [package=lipo-1000]
  A2 = battery capcity indicator module 1s-8s [package=THT]
  S1 = Round Pushbutton
  S2 = Round Pushbutton
  S3 = Round Pushbutton
  R26 = Resistor [tolerance=±5% resistance=220 package="1206 [SMD]"]
  LED1 = LED - 3mm [color="Red (633nm)" current=0.030A package="3 mm [THT]"]
  R27 = Resistor [tolerance=±5% resistance=220 package="1206 [SMD]"]
  R28 = Resistor [tolerance=±5% resistance=220 package="1206 [SMD]"]
  R29 = Basic Flex Resistor
  R30 = Resistor [tolerance=±5% resistance=220 package="0805 [SMD]"]
  S4 = Round Pushbutton
  LED2 = LED - 3mm [color="Red (633nm)" current=0.030A package="3 mm [THT]"]
  R31 = Resistor [tolerance=±5% resistance=220 package="1206 [SMD]"]
  LED3 = LED - 3mm [color="Red (633nm)" current=0.030A package="3 mm [THT]"]
  LED4 = LED - 3mm [color="Red (633nm)" current=0.030A package="3 mm [THT]"]
  R32 = Resistor [tolerance=±5% resistance=220 package="1206 [SMD]"]
  R33 = Resistor [tolerance=±5% resistance=220 package="1206 [SMD]"]

nets:
  N1: R1.Pin_1, Componente1.C4, R6.Pin_0
  GND: R1.Pin_2, R2.Pin_2, Componente1.GND, Componente1.EN, Componente2.GND, A1.Pin_15, R3.Pin_2, R4.Pin_2, R5.Pin_2, R11.Pin_2, R12.Pin_2, Componente3.GND, Componente3.EN, R15.leg1, R16.leg1, R17.leg1, R18.leg1, R19.leg1, R20.leg1, R21.leg1, R22.leg1, R23.leg1, R24.leg1, C2.2, C3.1, R25.leg1, TP1.pin6, S2.leg1, S3.leg1, R27.Pin_0, R29.Pin_2, S4.leg1, LED2.cathode, LED3.cathode, LED4.cathode
  N2: R2.pin_1, Componente1.C1, R10.Pin_0
  N3: Componente1.C0, R3.pin_1, R9.Pin_0
  N4: Componente1.C2, R4.pin_1, R6.Pin_1, R8.Pin_0, R13.Pin_1, R14.Pin_1, R30.Pin_1
  N5: Componente1.C3, R29.Pin_1, R30.Pin_0
  N6: Componente1.C5, R11.Pin_1, R13.Pin_0
  N7: Componente1.C6, R12.Pin_1, R14.Pin_0
  N8: Componente1.C7, R20.wiper
  N9: Componente1.C8, R24.wiper
  N10: Componente1.C9, R21.wiper
  N11: Componente1.C10, R23.wiper
  N12: Componente1.C11, R22.wiper
  N13: Componente1.C13, R5.pin_1, R7.Pin_0
  VCC: Componente1.VCC, Componente2.VDD, A1.Pin_14, R7.Pin_1, R8.Pin_1, R9.Pin_1, R10.Pin_1, Componente3.VCC, R15.leg2, R16.leg2, R17.leg2, R18.leg2, R19.leg2, R20.leg2, R21.leg2, R22.leg2, R23.leg2, R24.leg2, C2.1, C3.2, R25.leg2
  N14: Componente1.S0, A1.Pin_6, Componente3.S0
  N15: Componente1.S1, A1.Pin_11, Componente3.S1
  N16: Componente1.S2, A1.Pin_12, Componente3.S2
  N17: Componente1.S3, A1.Pin_13, Componente3.S3
  N18: Componente1.SIG, Componente2.A0
  N19: Componente2.SCL, A1.Pin_5
  N20: Componente2.SDA, A1.Pin_4
  N21: Componente2.A1, Componente3.SIG
  N22: Componente2.A2, R27.Pin_1, R28.Pin_0
  N23: A1.Pin_1, S2.leg0
  N24: A1.Pin_2, R32.Pin_1
  N25: A1.Pin_3, S3.leg0
  N26: A1.Pin_7, R33.Pin_1
  N27: A1.Pin_8, S4.leg0
  N28: A1.Pin_9, R31.Pin_1
  N29: A1.Pin_16, TP1.pin3, R26.Pin_1
  N30: Componente3.C1, R19.wiper
  N31: Componente3.C2, R18.wiper
  N32: Componente3.C3, R16.wiper
  N33: Componente3.C4, R15.wiper
  N34: Componente3.C5, R17.wiper
  N35: TP1.pin4, A2.pin1, S1.leg1, R28.Pin_1
  N36: TP1.pin5, U1.-, A2.pin2, LED1.cathode
  N37: U1.+, S1.leg0
  N38: R26.Pin_0, LED1.anode
  N39: LED2.anode, R31.Pin_0
  N40: LED3.anode, R32.Pin_0
  N41: LED4.anode, R33.Pin_0

notes:
  Circuito guante
  D1
  D2
  D3
  D4
  D5
  M1
  M2
  P0
  P1
  P2
  P3
  P4
  P5
  Ads1115
  CD74hc4067
  ESP32-C3
  POTENCIOMETROS
  SENSORES FLEX DEDOS
  NOTA: P5 opcional (mov rotacional de muñeca)
  En caso de utilizarse se necesita otro PCA9685
  SENSORES FLEX MUÑECA
  SENSORES MOVIMIENTO DE ABDUCCION
  TP4056 + Step-Up
  3,7 v - 1000 mAh
  5 v
  Encendido
  10 kΩ
  PARADA
  HOME
  CALIBRACIÓN
  BOTONES

custom parts:
  ADS1115: ADC ADS1115
  Esp32-c3 super mini: ESP32-C3 Development Board ESP32 SuperMini Development Board ESP32 Development Board WiFi Bluetooth.
  TP4056: A DIP stand-in part for whatever IC you want. With 6 pins on a 300mil dual inline package (DIP) footprint.
  battery capcity indicator module 1s-8s: battery capcity indicator module 1s-8s.
