# Fritzing sketch Circuito_mano_robot (saved by Fritzing 1.0.5)

parts:
  Componente1 = Adafruit PCA9685 PWM/Servo Breakout [part_number=815]
  Power_plug1 = Power plug
  M1 = DOIT Esp32 DevKit v1 (30 pins long, 11 pins width) [part_number=ESP32S-PIN30]
  C3 = Capacitor Polarized [package=nippon_f80]
  J2 = Basic Servo
  J3 = Basic Servo
  J4 = Basic Servo
  J5 = Basic Servo
  J6 = Basic Servo
  J7 = Basic Servo
  J8 = Basic Servo
  J9 = Basic Servo
  J10 = Basic Servo
  J11 = Basic Servo
  J12 = Basic Servo
  J13 = Basic Servo
  J14 = Basic Servo
  J15 = Basic Servo
  J16 = Basic Servo
  J17 = Basic Servo
  C4 = Capacitor Polarized [package=nippon_f80]
  C5 = Capacitor Polarized [package=nippon_f80]
  C6 = Capacitor Polarized [package=nippon_f80]
  C7 = Electrolytic Capacitor [capacitance=1μF voltage=35V package="0405 [SMD, electrolytic]"]
  Componente2 = Voltage Sensor 25V
  D1 = Diode [package=diode-1n4001]
  C8 = Capacitor Polarized [package=nippon_f80]
  C9 = Capacitor [package=cap-pth-small2]  # not connected

nets:
  VCC: Componente1.PWRIN, Power_plug1.VCC, C3.+, C4.+, C5.+, C6.+, Componente2.VCC, Componente2.+
  GND: Componente1.GND, Power_plug1.GND, M1.GND, C3.-, J2.gnd, J3.gnd, J4.gnd, J5.gnd, J6.gnd, J7.gnd, J8.gnd, J9.gnd, J10.gnd, J11.gnd, J12.gnd, J13.gnd, J14.gnd, J15.gnd, J16.gnd, J17.gnd, C4.-, C5.-, C6.-, C7.-, Componente2.GND, Componente2.-
  N1: Componente1.PWM7, J11.pulse
  VCC_2: Componente1.5.0V, Componente1.VCC, J2.vcc, J3.vcc, J4.vcc, J5.vcc, J6.vcc, J7.vcc, J8.vcc, J9.vcc, J10.vcc, J11.vcc, J12.vcc, J13.vcc, J14.vcc, J15.vcc, J16.vcc, J17.vcc
  N2: Componente1.PWM6, J9.pulse
  N3: Componente1.PWM5, J5.pulse
  N4: Componente1.PWM4, J8.pulse
  N5: Componente1.PWM3, J4.pulse
  N6: Componente1.PWM2, J2.pulse
  N7: Componente1.PWM1, J3.pulse
  N8: Componente1.PWM0, J14.pulse
  N9: Componente1.SDA, M1.D21
  N10: Componente1.SCL, M1.D22
  N11: Componente1.PWM15, J17.pulse
  N12: Componente1.PWM14, J16.pulse
  N13: Componente1.PWM13, J15.pulse
  N14: Componente1.PWM12, J12.pulse
  N15: Componente1.PWM11, J10.pulse
  N16: Componente1.PWM10, J7.pulse
  N17: Componente1.PWM9, J13.pulse
  N18: Componente1.PWM8, J6.pulse
  N19: M1.EN, C7.+
  N20: M1.D34, Componente2.S
  N21: D1.C, C8.+

notes:
  Circuito mano robot
  ESP-32
  PCA9685
  FUENTE
  SERVOS
  S1
  S2
  S3
  S4
  S5
  S6
  S7
  S8
  S9
  S10
  S11
  S12
  S13
  S14
  S15
  S16
  2200µF/16V
  MG90S
  DS3225
  MG92B
  Cable 12 AWG
  10µF/16V
  100nF
  1N5819

custom parts:
  Adafruit PCA9685 PWM/Servo Breakout: Using only two pins, control 16 free-running PWM outputs! I2C-controlled PWM driver with a built in clock. Unlike the TLC5940 family, you do not need to continuously send it signal tying up your microcontroller, its completely free running! 5V compliant, which means you can control it from a 3.3V microcontroller and still safely drive up to 6V outputs (this is good for when you want to control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
  DOIT Esp32 DevKit v1 (30 pins long, 11 pins width): The DOIT Esp32 DevKit v1 is one of the development board created by DOIT to evaluate the ESP-WROOM-32 module. It is based on the ESP32 microcontroller that boasts Wifi, Bluetooth, Ethernet and Low Power support all in a single chip. (vanepp) made breadboard work, adjusted pin numbering and labels and reduced size of schematic and cleaned up pcb. This chip is 30pins long (2 x15) and 11 pins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
