# Fritzing sketch Untitled Sketch (saved by Fritzing 1.0.5)

parts:
  Componente1 = Adafruit PCA9685 PWM/Servo Breakout [part_number=815]
  Power_plug1 = Power plug
  J1 = Basic Servo
  M1 = DOIT Esp32 DevKit v1 (30 pins long, 11 pins width) [part_number=ESP32S-PIN30]
  C3 = Capacitor Polarized [package=nippon_f80]  # not connected
  J2 = Basic Servo  # not connected
  J3 = Basic Servo  # not connected
  J4 = Basic Servo  # not connected
  J5 = Basic Servo  # not connected
  J6 = Basic Servo  # not connected
  J7 = Basic Servo  # not connected
  J8 = Basic Servo  # not connected
  J9 = Basic Servo  # not connected
  J10 = Basic Servo  # not connected
  J11 = Basic Servo  # not connected
  J12 = Basic Servo  # not connected
  J13 = Basic Servo  # not connected

nets:
  N1: Componente1.PWRIN, Power_plug1.VCC
  GND: Componente1.GND, Power_plug1.GND, J1.gnd, M1.GND
  N2: Componente1.PWM0, J1.pulse
  N3: Componente1.5.0V, J1.vcc
  VCC: Componente1.VCC, M1.3V3
  N4: Componente1.SDA, M1.D21
  N5: Componente1.SCL, M1.D22

custom parts:
  Adafruit PCA9685 PWM/Servo Breakout: Using only two pins, control 16 free-running PWM outputs! I2C-controlled PWM driver with a built in clock. Unlike the TLC5940 family, you do not need to continuously send it signal tying up your microcontroller, its completely free running! 5V compliant, which means you can control it from a 3.3V microcontroller and still safely drive up to 6V outputs (this is good for when you want to control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
  DOIT Esp32 DevKit v1 (30 pins long, 11 pins width): The DOIT Esp32 DevKit v1 is one of the development board created by DOIT to evaluate the ESP-WROOM-32 module. It is based on the ESP32 microcontroller that boasts Wifi, Bluetooth, Ethernet and Low Power support all in a single chip. (vanepp) made breadboard work, adjusted pin numbering and labels and reduced size of schematic and cleaned up pcb. This chip is 30pins long (2 x15) and 11 pins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
